// Logisim project Multiplication_Logic_Project_Final_Version.circ as structural Verilog: 2 circuits, main circuit Multiplication
module Multiplication (
  input  AS,
  input  A2,
  input  A1,
  input  BS,
  input  B2,
  input  B1,
  output _1,
  output Zero,
  output _2,
  output _3,
  output _4,
  output Negative
);

  wire and_1_out, and_2_out, and_3_out, half_adder_1_carry, n7_segment_display_driver_1_p5,
       n7_segment_display_driver_1_p6, n7_segment_display_driver_1_p7, n7_segment_display_driver_1_p8,
       n7_segment_display_driver_1_p9, n7_segment_display_driver_1_p10, n7_segment_display_driver_1_p11,
       nor_1_out, nor_2_out, not_1_out, xor_1_out;

  and and_1 (and_1_out, A1, B2);
  and and_2 (and_2_out, B1, A2);
  and and_3 (and_3_out, A2, B2);
  xor xor_1 (xor_1_out, BS, AS);
  and and_4 (_1, A1, B1);
  HALF_ADDER half_adder_1 (.A(and_1_out), .B(and_2_out), .SUM(_2), .CARRY(half_adder_1_carry));
  HALF_ADDER half_adder_2 (.A(half_adder_1_carry), .B(and_3_out), .SUM(_3), .CARRY(_4));
  // _7_segment_display_driver 7_segment_display_driver_1: pin names not known; wires that end beside it: _4, _3, _2, _1, n7_segment_display_driver_1_p5, n7_segment_display_driver_1_p6, n7_segment_display_driver_1_p7, n7_segment_display_driver_1_p8, n7_segment_display_driver_1_p9, n7_segment_display_driver_1_p10, n7_segment_display_driver_1_p11
  nor nor_1 (nor_1_out, _1, _2);
  and and_5 (Zero, nor_1_out, nor_2_out);
  nor nor_2 (nor_2_out, _3, _4);
  not not_1 (not_1_out, Zero);
  and and_6 (Negative, xor_1_out, not_1_out);
  _7_Segment_Display u_7_segment_display_1 (
    .g(n7_segment_display_driver_1_p11), .f(n7_segment_display_driver_1_p10),
    .a(n7_segment_display_driver_1_p5), .b(n7_segment_display_driver_1_p6),
    .e(n7_segment_display_driver_1_p9), .d(n7_segment_display_driver_1_p8), .c(n7_segment_display_driver_1_p7));  // open: dp
  _7_Segment_Display u_7_segment_display_2 (.g(Negative));  // open: f, a, b, e, d, c, dp
  LED u_Zero (.in(Zero));
  LED u_Negative (.in(Negative));
  LED Div__by_Zero (.in(1'b0));

  // Notes on the sheet:
  //   7-Segment-Decoder
  //   Result
endmodule

module HALF_ADDER (
  input  A,
  input  B,
  output SUM,
  output CARRY
);

  xor xor_1 (SUM, A, B);
  and and_1 (CARRY, A, B);
endmodule
